// Logisim project cpu.circ as structural Verilog: 1 circuit, main circuit main
module main (
  input  clock_run,
  input  clock_halt,
  input  in_3,
  input  in_4,
  input  [7:0] data_in,
  input  [15:0] addr_in,
  input  ip_to_addr,
  input  ip_hi_to_data,
  input  ip_lo_to_data,
  input  ip_inc,
  input  data_to_ip_lo,
  input  data_to_ip_hi,
  input  addr_to_ip,
  input  data_to_ir,
  output clock_halt_2,
  output clock_inv,
  output clock,
  output [7:0] data,
  output [15:0] addr,
  output [15:0] ip,
  output [7:0] ip_lo,
  output [7:0] ip_hi,
  output [7:0] out_23
);

  wire and_1_out, and_2_out, and_3_out, and_4_out, and_6_out, clock_1_out, clock_step_out, counter_2_carry,
       counter_3_carry, counter_4_carry, ip_reset_out, nor_1_out, nor_2_out, nor_3_out, not_1_out, not_2_out,
       or_1_out, or_2_out, or_3_out, or_4_out, or_5_out, or_6_out;
  wire [3:0] controlled_buffer_5_out;
  wire [15:4] controlled_buffer_5_out_2;

  assign data = in_3 ? data_in : 8'bz;  // Controlled_Buffer controlled_buffer_1
  assign data = ip_hi_to_data ? ip[15:8] : 8'bz;  // Controlled_Buffer controlled_buffer_2
  assign data = ip_lo_to_data ? ip[7:0] : 8'bz;  // Controlled_Buffer controlled_buffer_3
  Counter #(.width(4), .max('hf)) counter_1 (
    .load(or_2_out), .D(controlled_buffer_5_out_2[15:12]), .count(ip_inc), .Q(ip[15:12]), .clk(or_1_out),
    .clr(ip_reset_out));  // open: carry
  or or_1 (or_1_out, nor_1_out, and_1_out);
  assign controlled_buffer_5_out_2[15:8] = data_to_ip_hi ? data : 8'bz;  // Controlled_Buffer controlled_buffer_4
  assign {controlled_buffer_5_out_2[7:4], controlled_buffer_5_out} = data_to_ip_lo ? data : 8'bz;  // Controlled_Buffer controlled_buffer_5
  nor nor_1 (nor_1_out, counter_2_carry, or_2_out);
  Button clock_step (.out(clock_step_out));
  and and_1 (and_1_out, or_2_out, clock);
  or or_2 (or_2_out, data_to_ip_hi, addr_to_ip);
  or or_3 (or_3_out, data_to_ip_lo, addr_to_ip);
  Clock clock_1 (.out(clock_1_out));
  not not_1 (not_1_out, clock_run);
  Counter #(.width(4), .max('hf)) counter_2 (
    .load(or_2_out), .D(controlled_buffer_5_out_2[11:8]), .count(ip_inc), .Q(ip[11:8]),
    .carry(counter_2_carry), .clk(or_4_out), .clr(ip_reset_out));
  Register register_1 (.D(data), .en(data_to_ir), .Q(out_23), .clk(clock));  // open: clr
  and and_2 (and_2_out, clock_1_out, clock_run);
  and and_3 (and_3_out, not_1_out, clock_step_out);
  not not_2 (not_2_out, clock_halt);
  or or_4 (or_4_out, nor_2_out, and_4_out);
  or or_5 (or_5_out, and_2_out, and_3_out);
  nor nor_2 (nor_2_out, counter_3_carry, or_2_out);
  and and_4 (and_4_out, or_2_out, clock);
  and and_5 (clock, or_5_out, not_2_out);
  not not_3 (clock_inv, clock);
  Counter #(.width(4), .max('hf)) counter_3 (
    .load(or_3_out), .D(controlled_buffer_5_out_2[7:4]), .count(ip_inc), .Q(ip[7:4]),
    .carry(counter_3_carry), .clk(or_6_out), .clr(ip_reset_out));
  or or_6 (or_6_out, nor_3_out, and_6_out);
  nor nor_3 (nor_3_out, counter_4_carry, or_3_out);
  and and_6 (and_6_out, or_3_out, clock);
  Counter #(.width(4), .max('hf)) counter_4 (
    .load(or_3_out), .D(controlled_buffer_5_out), .count(ip_inc), .Q(ip[3:0]), .carry(counter_4_carry),
    .clk(clock), .clr(ip_reset_out));
  assign addr = in_4 ? addr_in : 16'bz;  // Controlled_Buffer controlled_buffer_6
  assign addr = ip_to_addr ? ip : 16'bz;  // Controlled_Buffer controlled_buffer_7
  assign {controlled_buffer_5_out_2, controlled_buffer_5_out} = addr_to_ip ? addr : 16'bz;  // Controlled_Buffer controlled_buffer_8
  Button ip_reset (.out(ip_reset_out));

  assign clock_halt_2 = clock_halt;
  assign ip_hi = ip[15:8];
  assign ip_lo = ip[7:0];

  // Notes on the sheet:
  //   8-Bit Data Bus
  //   Program Counter
  //   Clock
  //   Instruction Register
  //   Instruction Pointer
  //   16-Bit Address Bus
endmodule
